// Logisim project Arithmetic_.circ as structural Verilog
module XOR (
  input  in_1,
  input  in_2,
  output out_3
);

  wire and_1_out, and_2_out, not_1_out, not_2_out;

  not not_1 (not_1_out, in_1);
  not not_2 (not_2_out, in_2);
  and and_1 (and_1_out, not_1_out, in_2);
  and and_2 (and_2_out, in_1, not_2_out);
  or or_1 (out_3, and_1_out, and_2_out);
endmodule

module NAND (
  input  in_1,
  input  in_2,
  output out_3
);

  wire and_1_out;

  and and_1 (and_1_out, in_1, in_2);
  not not_1 (out_3, and_1_out);
endmodule

module NOR (
  input  in_1,
  input  in_2
);

  wire not_1_out, or_1_out;

  not not_1 (not_1_out, or_1_out);
  or or_1 (or_1_out, in_1, in_2);
endmodule

module Half_Adder (
  input  A,
  input  B,
  output Sum_Out,
  output Carry_Out
);

  xor xor_1 (Sum_Out, A, B);
  and and_1 (Carry_Out, A, B);
endmodule

module Full_Adder (
  input  CI,
  input  A,
  input  B,
  output Sum_Out,
  output Carry_Out
);

  wire half_adder_1_carry_out, half_adder_1_sum_out, half_adder_2_carry_out;

  Half_Adder half_adder_1 (.A(A), .B(B), .Sum_Out(half_adder_1_sum_out), .Carry_Out(half_adder_1_carry_out));
  Half_Adder half_adder_2 (.A(CI), .B(half_adder_1_sum_out), .Sum_Out(Sum_Out), .Carry_Out(half_adder_2_carry_out));
  or or_1 (Carry_Out, half_adder_2_carry_out, half_adder_1_carry_out);
endmodule

module Eight_Bit_Adder (
  input  CI,
  input  [7:0] A,
  input  [7:0] B,
  output [7:0] SO,
  output CO
);

  wire full_adder_1_carry_out, full_adder_2_carry_out, full_adder_3_carry_out, full_adder_4_carry_out,
       full_adder_5_carry_out, full_adder_6_carry_out, full_adder_7_carry_out;

  Full_Adder full_adder_1 (.CI(CI), .A(A[0]), .B(B[0]), .Sum_Out(SO[0]), .Carry_Out(full_adder_1_carry_out));
  Full_Adder full_adder_2 (
    .CI(full_adder_1_carry_out), .A(A[1]), .B(B[1]), .Sum_Out(SO[1]), .Carry_Out(full_adder_2_carry_out));
  Full_Adder full_adder_3 (
    .CI(full_adder_2_carry_out), .A(A[2]), .B(B[2]), .Sum_Out(SO[2]), .Carry_Out(full_adder_3_carry_out));
  Full_Adder full_adder_4 (
    .CI(full_adder_3_carry_out), .A(A[3]), .B(B[3]), .Sum_Out(SO[3]), .Carry_Out(full_adder_4_carry_out));
  Full_Adder full_adder_5 (
    .CI(full_adder_4_carry_out), .A(A[4]), .B(B[4]), .Sum_Out(SO[4]), .Carry_Out(full_adder_5_carry_out));
  Full_Adder full_adder_6 (
    .CI(full_adder_5_carry_out), .A(A[5]), .B(B[5]), .Sum_Out(SO[5]), .Carry_Out(full_adder_6_carry_out));
  Full_Adder full_adder_7 (
    .CI(full_adder_6_carry_out), .A(A[6]), .B(B[6]), .Sum_Out(SO[6]), .Carry_Out(full_adder_7_carry_out));
  Full_Adder full_adder_8 (.CI(full_adder_7_carry_out), .A(A[7]), .B(B[7]), .Sum_Out(SO[7]), .Carry_Out(CO));
endmodule

module ALU (
  input  CI,
  input  [7:0] A,
  input  [7:0] B,
  input  Sub,
  output [7:0] SO,
  output CO
);

  wire or_1_out;
  wire [7:0] multiplexer_1_out, not_1_out;

  or or_1 (or_1_out, CI, Sub);
  assign not_1_out = ~B;  // NOT_Gate not_1, 8 bits wide
  Multiplexer #(.width(8), .enable("false")) multiplexer_1 (
    .in0(B), .in1(not_1_out), .out(multiplexer_1_out), .sel(Sub));
  Eight_Bit_Adder eight_bit_adder_1 (.CI(or_1_out), .A(A), .B(multiplexer_1_out), .SO(SO), .CO(CO));
endmodule
