// Logisim project Memory_.circ as structural Verilog
module RS_flip_flop (
  input  R,
  input  S,
  output Q,
  output NotQ
);

  nor nor_1 (Q, R, NotQ);
  nor nor_2 (NotQ, Q, S);
endmodule

module Level_Triggered_D_latch (
  input  Clear,
  input  Clock,
  input  Data,
  output Q,
  output NotQ
);

  wire and_1_out, and_2_out, not_1_out, or_1_out;

  not not_1 (not_1_out, Data);
  and and_1 (and_1_out, Clock, not_1_out);
  and and_2 (and_2_out, Clock, Data);
  or or_1 (or_1_out, Clear, and_1_out);
  RS_flip_flop rs_flip_flop_1 (.R(or_1_out), .S(and_2_out), .Q(Q), .NotQ(NotQ));
endmodule

module eight_bit_latch (
  input  Clear,
  input  [7:0] Eight_Bit_data,
  input  Clock,
  output [7:0] Data_Output
);

  Level_Triggered_D_latch level_triggered_d_latch_1 (
    .Clock(Clock), .Data(Eight_Bit_data[0]), .Q(Data_Output[0]), .Clear(Clear));  // open: NotQ
  Level_Triggered_D_latch level_triggered_d_latch_2 (
    .Clock(Clock), .Data(Eight_Bit_data[1]), .Q(Data_Output[1]), .Clear(Clear));  // open: NotQ
  Level_Triggered_D_latch level_triggered_d_latch_3 (
    .Clock(Clock), .Data(Eight_Bit_data[2]), .Q(Data_Output[2]), .Clear(Clear));  // open: NotQ
  Level_Triggered_D_latch level_triggered_d_latch_4 (
    .Clock(Clock), .Data(Eight_Bit_data[3]), .Q(Data_Output[3]), .Clear(Clear));  // open: NotQ
  Level_Triggered_D_latch level_triggered_d_latch_5 (
    .Clock(Clock), .Data(Eight_Bit_data[4]), .Q(Data_Output[4]), .Clear(Clear));  // open: NotQ
  Level_Triggered_D_latch level_triggered_d_latch_6 (
    .Clock(Clock), .Data(Eight_Bit_data[5]), .Q(Data_Output[5]), .Clear(Clear));  // open: NotQ
  Level_Triggered_D_latch level_triggered_d_latch_7 (
    .Clock(Clock), .Data(Eight_Bit_data[6]), .Q(Data_Output[6]), .Clear(Clear));  // open: NotQ
  Level_Triggered_D_latch level_triggered_d_latch_8 (
    .Clock(Clock), .Data(Eight_Bit_data[7]), .Q(Data_Output[7]), .Clear(Clear));  // open: NotQ
endmodule

module Two_One_Selector (
  input  A,
  input  Sel,
  input  B,
  output out_4
);

  wire and_1_out, and_2_out, not_1_out;

  not not_1 (not_1_out, Sel);
  and and_1 (and_1_out, A, Sel);
  and and_2 (and_2_out, not_1_out, B);
  or or_1 (out_4, and_1_out, and_2_out);

  // Notes on the sheet:
  //   If Sel is 1, then select A
endmodule

module Multi_Input_Adder (
  input  [7:0] A,
  input  Clear_Latch,
  input  Add,
  output [7:0] Saved_Result
);

  wire [7:0] eight_bit_adder_1_so;

  Eight_Bit_Adder eight_bit_adder_1 (.CI(1'b0), .A(A), .B(Saved_Result), .SO(eight_bit_adder_1_so));  // open: CO
  eight_bit_latch eight_bit_latch_1 (
    .Eight_Bit_data(eight_bit_adder_1_so), .Clock(Add), .Data_Output(Saved_Result), .Clear(Clear_Latch));
endmodule

module Two_One_Selector_Eight_Bit (
  input  Sel,
  input  [7:0] A,
  input  [7:0] B,
  output [7:0] Out
);

  Two_One_Selector two_one_selector_1 (.A(A[0]), .Sel(Sel), .B(B[0]), .out_4(Out[0]));
  Two_One_Selector two_one_selector_2 (.A(A[1]), .Sel(Sel), .B(B[1]), .out_4(Out[1]));
  Two_One_Selector two_one_selector_3 (.A(A[2]), .Sel(Sel), .B(B[2]), .out_4(Out[2]));
  Two_One_Selector two_one_selector_4 (.A(A[3]), .Sel(Sel), .B(B[3]), .out_4(Out[3]));
  Two_One_Selector two_one_selector_5 (.A(A[4]), .Sel(Sel), .B(B[4]), .out_4(Out[4]));
  Two_One_Selector two_one_selector_6 (.A(A[5]), .Sel(Sel), .B(B[5]), .out_4(Out[5]));
  Two_One_Selector two_one_selector_7 (.A(A[6]), .Sel(Sel), .B(B[6]), .out_4(Out[6]));
  Two_One_Selector two_one_selector_8 (.A(A[7]), .Sel(Sel), .B(B[7]), .out_4(Out[7]));
endmodule

module Edge_Triggered_DLatch (
  input  Clock,
  input  Data,
  input  Clear,
  output Q,
  output NotQ
);

  wire level_triggered_d_latch_1_q, not_1_out;

  not not_1 (not_1_out, Clock);
  Level_Triggered_D_latch level_triggered_d_latch_1 (
    .Clock(not_1_out), .Data(Data), .Q(level_triggered_d_latch_1_q));  // open: NotQ, Clear
  Level_Triggered_D_latch level_triggered_d_latch_2 (
    .Clock(Clock), .Data(level_triggered_d_latch_1_q), .Q(Q), .NotQ(NotQ), .Clear(Clear));
endmodule

module Frequency_Divider (
  input  Clear,
  output out_2
);

  wire clock_1_out, edge_triggered_dlatch_1_notq;

  Clock clock_1 (.out(clock_1_out));
  Edge_Triggered_DLatch edge_triggered_dlatch_1 (
    .Clock(clock_1_out), .Q(out_2), .Data(edge_triggered_dlatch_1_notq), .NotQ(edge_triggered_dlatch_1_notq),
    .Clear(Clear));
endmodule

module Oscillator (
  input  in_1,
  output out_2
);

  not not_1 (in_1, in_1);

  assign out_2 = in_1;
endmodule

module Eight_Bit_Ripple_Counter (
  input  Clear,
  output [7:0] out_2
);

  wire clock_1_out, edge_triggered_dlatch_1_notq, edge_triggered_dlatch_2_notq, edge_triggered_dlatch_3_notq,
       edge_triggered_dlatch_4_notq, edge_triggered_dlatch_5_notq, edge_triggered_dlatch_6_notq,
       edge_triggered_dlatch_7_notq, edge_triggered_dlatch_8_notq;

  Clock clock_1 (.out(clock_1_out));
  Edge_Triggered_DLatch edge_triggered_dlatch_1 (
    .Clock(clock_1_out), .Q(out_2[0]), .Data(edge_triggered_dlatch_1_notq),
    .NotQ(edge_triggered_dlatch_1_notq), .Clear(Clear));
  Edge_Triggered_DLatch edge_triggered_dlatch_2 (
    .Clock(edge_triggered_dlatch_1_notq), .Q(out_2[1]), .Data(edge_triggered_dlatch_2_notq),
    .NotQ(edge_triggered_dlatch_2_notq), .Clear(Clear));
  Edge_Triggered_DLatch edge_triggered_dlatch_3 (
    .Clock(edge_triggered_dlatch_2_notq), .Q(out_2[2]), .Data(edge_triggered_dlatch_3_notq),
    .NotQ(edge_triggered_dlatch_3_notq), .Clear(Clear));
  Edge_Triggered_DLatch edge_triggered_dlatch_4 (
    .Clock(edge_triggered_dlatch_3_notq), .Q(out_2[3]), .Data(edge_triggered_dlatch_4_notq),
    .NotQ(edge_triggered_dlatch_4_notq), .Clear(Clear));
  Edge_Triggered_DLatch edge_triggered_dlatch_5 (
    .Clock(edge_triggered_dlatch_4_notq), .Q(out_2[4]), .Data(edge_triggered_dlatch_5_notq),
    .NotQ(edge_triggered_dlatch_5_notq), .Clear(Clear));
  Edge_Triggered_DLatch edge_triggered_dlatch_6 (
    .Clock(edge_triggered_dlatch_5_notq), .Q(out_2[5]), .Data(edge_triggered_dlatch_6_notq),
    .NotQ(edge_triggered_dlatch_6_notq), .Clear(Clear));
  Edge_Triggered_DLatch edge_triggered_dlatch_7 (
    .Clock(edge_triggered_dlatch_6_notq), .Q(out_2[6]), .Data(edge_triggered_dlatch_7_notq),
    .NotQ(edge_triggered_dlatch_7_notq), .Clear(Clear));
  Edge_Triggered_DLatch edge_triggered_dlatch_8 (
    .Clock(edge_triggered_dlatch_7_notq), .Q(out_2[7]), .Data(edge_triggered_dlatch_8_notq),
    .NotQ(edge_triggered_dlatch_8_notq), .Clear(Clear));
endmodule

module Eight_Bit_Edge_Triggered_DLatch (
  input  Clear,
  input  [7:0] Eight_Bit_data,
  input  Clock,
  output [7:0] Data_Output
);

  Edge_Triggered_DLatch edge_triggered_dlatch_1 (
    .Clock(Clock), .Q(Data_Output[0]), .Data(Eight_Bit_data[0]), .Clear(Clear));  // open: NotQ
  Edge_Triggered_DLatch edge_triggered_dlatch_2 (
    .Clock(Clock), .Q(Data_Output[1]), .Data(Eight_Bit_data[1]), .Clear(Clear));  // open: NotQ
  Edge_Triggered_DLatch edge_triggered_dlatch_3 (
    .Clock(Clock), .Q(Data_Output[2]), .Data(Eight_Bit_data[2]), .Clear(Clear));  // open: NotQ
  Edge_Triggered_DLatch edge_triggered_dlatch_4 (
    .Clock(Clock), .Q(Data_Output[3]), .Data(Eight_Bit_data[3]), .Clear(Clear));  // open: NotQ
  Edge_Triggered_DLatch edge_triggered_dlatch_5 (
    .Clock(Clock), .Q(Data_Output[4]), .Data(Eight_Bit_data[4]), .Clear(Clear));  // open: NotQ
  Edge_Triggered_DLatch edge_triggered_dlatch_6 (
    .Clock(Clock), .Q(Data_Output[5]), .Data(Eight_Bit_data[5]), .Clear(Clear));  // open: NotQ
  Edge_Triggered_DLatch edge_triggered_dlatch_7 (
    .Clock(Clock), .Q(Data_Output[6]), .Data(Eight_Bit_data[6]), .Clear(Clear));  // open: NotQ
  Edge_Triggered_DLatch edge_triggered_dlatch_8 (
    .Clock(Clock), .Q(Data_Output[7]), .Data(Eight_Bit_data[7]), .Clear(Clear));  // open: NotQ
endmodule

module Multi_Input_Adder_Fixed (
  input  [7:0] A,
  input  Clear_Latch,
  input  Add,
  output [7:0] Current_Sum,
  output [7:0] Saved_Result
);

  Eight_Bit_Adder eight_bit_adder_1 (.CI(1'b0), .A(A), .B(Saved_Result), .SO(Current_Sum));  // open: CO
  Eight_Bit_Edge_Triggered_DLatch eight_bit_edge_triggered_dlatch_1 (
    .Clear(Clear_Latch), .Eight_Bit_data(Current_Sum), .Clock(Add), .Data_Output(Saved_Result));
endmodule

module Three_Eight_Decoder (
  input  Data,
  input  [2:0] Sel,
  output [7:0] Out
);

  wire not_1_out, not_2_out, not_3_out;

  not not_1 (not_1_out, Sel[0]);
  not not_2 (not_2_out, Sel[1]);
  not not_3 (not_3_out, Sel[2]);
  and and_1 (Out[0], Data, not_1_out, not_2_out, not_3_out);
  and and_2 (Out[1], Data, Sel[0], not_2_out, not_3_out);
  and and_3 (Out[2], Data, not_1_out, Sel[1], not_3_out);
  and and_4 (Out[3], Data, Sel[0], Sel[1], not_3_out);
  and and_5 (Out[4], Data, not_1_out, not_2_out, Sel[2]);
  and and_6 (Out[5], Data, Sel[0], not_2_out, Sel[2]);
  and and_7 (Out[6], Data, not_1_out, Sel[1], Sel[2]);
  and and_8 (Out[7], Data, Sel[0], Sel[1], Sel[2]);

  // Notes on the sheet:
  //   3 Selectors are used to select an output from 8 outputs
endmodule

module Eight_One_Selector (
  input  [7:0] Data,
  input  [2:0] Sel,
  output Output
);

  wire and_1_out, and_2_out, and_3_out, and_4_out, and_5_out, and_6_out, and_7_out, and_8_out, not_1_out,
       not_2_out, not_3_out;

  not not_1 (not_1_out, Sel[0]);
  not not_2 (not_2_out, Sel[1]);
  not not_3 (not_3_out, Sel[2]);
  and and_1 (and_1_out, Data[0], not_1_out, not_2_out, not_3_out);
  and and_2 (and_2_out, Data[1], Sel[0], not_2_out, not_3_out);
  and and_3 (and_3_out, Data[2], not_1_out, Sel[1], not_3_out);
  and and_4 (and_4_out, Data[3], Sel[0], Sel[1], not_3_out);
  and and_5 (and_5_out, Data[4], not_1_out, not_2_out, Sel[2]);
  and and_6 (and_6_out, Data[5], Sel[0], not_2_out, Sel[2]);
  and and_7 (and_7_out, Data[6], not_1_out, Sel[1], Sel[2]);
  and and_8 (and_8_out, Data[7], Sel[0], Sel[1], Sel[2]);
  or or_1 (Output, and_1_out, and_2_out, and_3_out, and_4_out, and_5_out, and_6_out, and_7_out, and_8_out);

  // Notes on the sheet:
  //   Because 8 values can be stored in 3 bits, we have 3 inputs for selectors which act as an address
  //   We combine each data bit with the corresponding selectors, by setting the nots on the selector to all be 1
endmodule

module Eight_By_One_RAM (
  input  Clear,
  input  Data,
  input  Write,
  input  [2:0] Address,
  output Out
);

  wire [7:0] level_triggered_d_latch_1_q, three_eight_decoder_1_out;

  Three_Eight_Decoder three_eight_decoder_1 (.Data(Write), .Sel(Address), .Out(three_eight_decoder_1_out));
  Level_Triggered_D_latch level_triggered_d_latch_1 (
    .Clock(three_eight_decoder_1_out[0]), .Data(Data), .Q(level_triggered_d_latch_1_q[0]), .Clear(Clear));  // open: NotQ
  Level_Triggered_D_latch level_triggered_d_latch_2 (
    .Clock(three_eight_decoder_1_out[1]), .Data(Data), .Q(level_triggered_d_latch_1_q[1]), .Clear(Clear));  // open: NotQ
  Level_Triggered_D_latch level_triggered_d_latch_3 (
    .Clock(three_eight_decoder_1_out[2]), .Data(Data), .Q(level_triggered_d_latch_1_q[2]), .Clear(Clear));  // open: NotQ
  Level_Triggered_D_latch level_triggered_d_latch_4 (
    .Clock(three_eight_decoder_1_out[3]), .Data(Data), .Q(level_triggered_d_latch_1_q[3]), .Clear(Clear));  // open: NotQ
  Level_Triggered_D_latch level_triggered_d_latch_5 (
    .Clock(three_eight_decoder_1_out[4]), .Data(Data), .Q(level_triggered_d_latch_1_q[4]), .Clear(Clear));  // open: NotQ
  Level_Triggered_D_latch level_triggered_d_latch_6 (
    .Clock(three_eight_decoder_1_out[5]), .Data(Data), .Q(level_triggered_d_latch_1_q[5]), .Clear(Clear));  // open: NotQ
  Level_Triggered_D_latch level_triggered_d_latch_7 (
    .Clock(three_eight_decoder_1_out[6]), .Data(Data), .Q(level_triggered_d_latch_1_q[6]), .Clear(Clear));  // open: NotQ
  Level_Triggered_D_latch level_triggered_d_latch_8 (
    .Clock(three_eight_decoder_1_out[7]), .Data(Data), .Q(level_triggered_d_latch_1_q[7]), .Clear(Clear));  // open: NotQ
  Eight_One_Selector eight_one_selector_1 (.Data(level_triggered_d_latch_1_q), .Sel(Address), .Output(Out));
endmodule

module Eight_Eight_RAM (
  input  [7:0] DI,
  input  Write,
  input  [2:0] Address,
  input  Clear,
  output [7:0] DO
);

  Eight_By_One_RAM eight_by_one_ram_1 (.Clear(Clear), .Data(DI[0]), .Write(Write), .Address(Address), .Out(DO[0]));
  Eight_By_One_RAM eight_by_one_ram_2 (.Clear(Clear), .Data(DI[1]), .Write(Write), .Address(Address), .Out(DO[1]));
  Eight_By_One_RAM eight_by_one_ram_3 (.Clear(Clear), .Data(DI[2]), .Write(Write), .Address(Address), .Out(DO[2]));
  Eight_By_One_RAM eight_by_one_ram_4 (.Clear(Clear), .Data(DI[3]), .Write(Write), .Address(Address), .Out(DO[3]));
  Eight_By_One_RAM eight_by_one_ram_5 (.Clear(Clear), .Data(DI[4]), .Write(Write), .Address(Address), .Out(DO[4]));
  Eight_By_One_RAM eight_by_one_ram_6 (.Clear(Clear), .Data(DI[5]), .Write(Write), .Address(Address), .Out(DO[5]));
  Eight_By_One_RAM eight_by_one_ram_7 (.Clear(Clear), .Data(DI[6]), .Write(Write), .Address(Address), .Out(DO[6]));
  Eight_By_One_RAM eight_by_one_ram_8 (.Clear(Clear), .Data(DI[7]), .Write(Write), .Address(Address), .Out(DO[7]));
endmodule

module Sixteen_Eight_RAM (
  input  [7:0] DI,
  input  Write,
  input  [3:0] Address,
  input  Clear,
  output [7:0] DO
);

  wire demultiplexer_1_out0, demultiplexer_1_out1;
  wire [7:0] eight_eight_ram_1_do, eight_eight_ram_2_do;

  Demultiplexer #(.enable("false")) demultiplexer_1 (
    .out0(demultiplexer_1_out0), .out1(demultiplexer_1_out1), .in(Write), .sel(Address[3]));
  Eight_Eight_RAM eight_eight_ram_1 (
    .DI(DI), .Write(demultiplexer_1_out0), .Address(Address[2:0]), .Clear(Clear), .DO(eight_eight_ram_1_do));
  Eight_Eight_RAM eight_eight_ram_2 (
    .DI(DI), .Write(demultiplexer_1_out1), .Address(Address[2:0]), .Clear(Clear), .DO(eight_eight_ram_2_do));
  Multiplexer #(.width(8), .enable("false")) multiplexer_1 (
    .in0(eight_eight_ram_1_do), .in1(eight_eight_ram_2_do), .out(DO), .sel(Address[3]));
endmodule
