// Logisim project Simulator_.circ as structural Verilog
module CPU (
  input  in_1,
  input  in_2,
  output [7:0] out_3,
  output [7:0] out_4
);

  wire alu_1_co, and_1_out, and_2_out, and_3_out, and_4_out, and_5_out, and_6_out, and_7_out, and_8_out,
       and_9_out, button_1_out, button_2_out, Carry_q, clock_1_out, d_ff_1_q, d_ff_2_q, d_ff_3_q,
       eight_bit_compare_1_out, eight_bit_compare_2_out, eight_bit_compare_3_out, eight_bit_compare_4_out,
       eight_bit_compare_5_out, eight_bit_compare_6_out, eight_bit_compare_7_out, eight_bit_compare_8_out,
       eight_bit_compare_9_out, eight_bit_compare_10_out, eight_bit_compare_11_out, eight_bit_compare_12_out,
       eight_bit_compare_13_out, eight_bit_compare_14_out, eight_bit_compare_15_out,
       eight_bit_compare_16_out, eight_bit_compare_17_out, eight_bit_compare_18_out,
       eight_bit_compare_19_out, eight_bit_compare_20_out, eight_bit_compare_21_out, not_1_out, not_2_out,
       not_3_out, not_4_out, or_1_out, or_2_out, or_3_out, or_4_out, or_5_out, or_6_out, or_7_out, or_8_out,
       or_9_out, or_10_out, or_11_out;
  wire [7:0] ACC_q, alu_1_so, B_q, CIR_q, Data_dout, demultiplexer_1_out0, demultiplexer_1_out1, MAR_q,
       MDR_q, multiplexer_1_out, multiplexer_2_out, multiplexer_3_out, multiplexer_4_out, multiplexer_5_out,
       multiplexer_6_out, multiplexer_7_out, Stack_Pointer_q;

  Button button_1 (.out(button_1_out));
  Clock clock_1 (.out(clock_1_out));
  or or_1 (or_1_out, and_3_out, and_4_out, and_5_out, and_6_out, eight_bit_compare_10_out);
  and and_1 (and_1_out, or_1_out, out_3[0]);
  and and_2 (and_2_out, clock_1_out, not_1_out);
  not not_1 (not_1_out, eight_bit_compare_3_out);
  Eight_Bit_Compare eight_bit_compare_1 (.A(CIR_q), .B(8'h11), .Out(eight_bit_compare_1_out));
  Eight_Bit_Compare eight_bit_compare_2 (.A(CIR_q), .B(8'h13), .Out(eight_bit_compare_2_out));
  or or_2 (or_2_out, eight_bit_compare_11_out, eight_bit_compare_5_out);
  and and_3 (and_3_out, not_4_out, eight_bit_compare_6_out);
  and and_4 (and_4_out, not_2_out, eight_bit_compare_7_out);
  and and_5 (and_5_out, Carry_q, eight_bit_compare_8_out);
  and and_6 (and_6_out, eight_bit_compare_12_out, eight_bit_compare_9_out);
  Eight_Bit_Counter eight_bit_counter_1 (
    .Set(and_1_out), .DI(MAR_q), .Clear(button_1_out), .Clock(and_2_out), .out_5(out_3));
  Eight_Bit_Compare eight_bit_compare_3 (.A({8{1'b1}}), .B(CIR_q), .Out(eight_bit_compare_3_out));
  or or_3 (or_3_out, eight_bit_compare_1_out, eight_bit_compare_11_out, eight_bit_compare_2_out);
  or or_4 (or_4_out, out_3[0], button_2_out);
  Multiplexer #(.width(8), .enable("false")) multiplexer_1 (
    .in0(MDR_q), .in1(ACC_q), .out(multiplexer_1_out), .sel(or_2_out));
  Eight_Bit_Compare eight_bit_compare_4 (.A(CIR_q), .B(8'h14), .Out(eight_bit_compare_4_out));
  Eight_Bit_Compare eight_bit_compare_5 (.A(8'h43), .B(CIR_q), .Out(eight_bit_compare_5_out));
  Eight_Bit_Compare eight_bit_compare_6 (.A(CIR_q), .B(8'h34), .Out(eight_bit_compare_6_out));
  not not_2 (not_2_out, eight_bit_compare_12_out);
  Eight_Bit_Compare eight_bit_compare_7 (.A(CIR_q), .B(8'h33), .Out(eight_bit_compare_7_out));
  Eight_Bit_Compare eight_bit_compare_8 (.A(8'h32), .B(CIR_q), .Out(eight_bit_compare_8_out));
  Eight_Bit_Compare eight_bit_compare_9 (.A(CIR_q), .B(8'h31), .Out(eight_bit_compare_9_out));
  Eight_Bit_Compare eight_bit_compare_10 (.A(CIR_q), .B(8'h30), .Out(eight_bit_compare_10_out));
  D_Flip_Flop #(.trigger("falling")) d_ff_1 (
    .D(1'b1), .clk(and_7_out), .Q(d_ff_1_q), .reset(or_4_out));  // open: Qn, preset
  and and_7 (and_7_out, out_3[0], or_3_out);
  D_Flip_Flop #(.trigger("falling")) d_ff_2 (
    .D(1'b1), .clk(eight_bit_compare_2_out), .Q(d_ff_2_q), .reset(or_4_out));  // open: Qn, preset
  Register #(.trigger("falling")) Stack_Pointer (
    .D(multiplexer_1_out), .en(1'b1), .clk(or_5_out), .Q(Stack_Pointer_q), .clr(button_2_out));
  or or_5 (or_5_out, eight_bit_compare_4_out, eight_bit_compare_5_out);
  D_Flip_Flop #(.trigger("falling")) d_ff_3 (
    .D(1'b1), .clk(eight_bit_compare_11_out), .Q(d_ff_3_q), .reset(or_4_out));  // open: Qn, preset
  Multiplexer #(.width(8), .enable("false")) multiplexer_2 (
    .in0(MAR_q), .in1(Stack_Pointer_q), .out(multiplexer_2_out), .sel(or_6_out));
  or or_6 (or_6_out, d_ff_3_q, eight_bit_compare_14_out);
  Eight_Bit_Compare eight_bit_compare_11 (.A(8'h15), .B(CIR_q), .Out(eight_bit_compare_11_out));
  Eight_Bit_Compare eight_bit_compare_12 (.A(ACC_q), .B({8{1'b0}}), .Out(eight_bit_compare_12_out));
  not not_3 (not_3_out, out_3[0]);
  RAM #(.trigger("high"), .databus("bibus")) Code (.addr(out_3), .we(1'b0), .oe(1'b1), .dout(out_4));  // open: din
  RAM #(.trigger("high"), .databus("bibus")) Data (
    .addr(multiplexer_2_out), .we(d_ff_1_q), .oe(1'b1), .din(multiplexer_3_out), .dout(Data_dout));
  Multiplexer #(.width(8), .enable("false")) multiplexer_3 (
    .in0(ACC_q), .in1(B_q), .out(multiplexer_3_out), .sel(d_ff_2_q));
  Eight_Bit_Compare eight_bit_compare_13 (.A(CIR_q), .B(8'h12), .Out(eight_bit_compare_13_out));
  Eight_Bit_Compare eight_bit_compare_14 (.A(CIR_q), .B(8'h16), .Out(eight_bit_compare_14_out));
  not not_4 (not_4_out, Carry_q);
  Register #(.trigger("falling")) B (.D(multiplexer_4_out), .en(1'b1), .clk(or_7_out), .Q(B_q), .clr(button_2_out));
  or or_7 (or_7_out, eight_bit_compare_13_out, eight_bit_compare_14_out, eight_bit_compare_15_out);
  Multiplexer #(.width(8), .enable("false")) multiplexer_4 (
    .in0(MDR_q), .in1(ACC_q), .out(multiplexer_4_out), .sel(eight_bit_compare_15_out));
  Eight_Bit_Compare eight_bit_compare_15 (.A(CIR_q), .B(8'h41), .Out(eight_bit_compare_15_out));
  Demultiplexer #(.width(8), .enable("false")) demultiplexer_1 (
    .out0(demultiplexer_1_out0), .out1(demultiplexer_1_out1), .in(out_4), .sel(out_3[0]));
  Button button_2 (.out(button_2_out));
  Register #(.trigger("high")) CIR (
    .D(demultiplexer_1_out0), .en(1'b1), .clk(not_3_out), .Q(CIR_q), .clr(button_2_out));
  Register #(.trigger("high")) MAR (.D(demultiplexer_1_out1), .en(1'b1), .clk(out_3[0]), .Q(MAR_q), .clr(button_2_out));
  Register #(.trigger("high")) MDR (.D(Data_dout), .en(1'b1), .clk(out_3[0]), .Q(MDR_q), .clr(button_2_out));
  or or_8 (or_8_out, eight_bit_compare_16_out, eight_bit_compare_21_out, eight_bit_compare_17_out);
  and and_8 (and_8_out, Carry_q, eight_bit_compare_21_out);
  ALU alu_1 (.A(ACC_q), .B(MDR_q), .Sub(eight_bit_compare_16_out), .SO(alu_1_so), .CO(alu_1_co), .CI(and_8_out));
  Eight_Bit_Compare eight_bit_compare_16 (.A(8'h21), .B(CIR_q), .Out(eight_bit_compare_16_out));
  Eight_Bit_Compare eight_bit_compare_17 (.A(CIR_q), .B(8'h20), .Out(eight_bit_compare_17_out));
  or or_9 (or_9_out, eight_bit_compare_17_out, eight_bit_compare_16_out, eight_bit_compare_19_out, eight_bit_compare_21_out);
  Multiplexer #(.width(8), .enable("false")) multiplexer_5 (
    .in0(MDR_q), .in1(alu_1_so), .out(multiplexer_5_out), .sel(or_8_out));
  Eight_Bit_Compare eight_bit_compare_18 (.A(8'h42), .B(CIR_q), .Out(eight_bit_compare_18_out));
  Eight_Bit_Compare eight_bit_compare_19 (.A(8'h10), .B(CIR_q), .Out(eight_bit_compare_19_out));
  Multiplexer #(.width(8), .enable("false")) multiplexer_6 (
    .in0(multiplexer_7_out), .in1(Stack_Pointer_q), .out(multiplexer_6_out), .sel(eight_bit_compare_18_out));
  Multiplexer #(.width(8), .enable("false")) multiplexer_7 (
    .in0(multiplexer_5_out), .in1(B_q), .out(multiplexer_7_out), .sel(eight_bit_compare_20_out));
  and and_9 (and_9_out, or_9_out, out_3[0]);
  Eight_Bit_Compare eight_bit_compare_20 (.A(8'h40), .B(CIR_q), .Out(eight_bit_compare_20_out));
  Eight_Bit_Compare eight_bit_compare_21 (.A(8'h22), .B(CIR_q), .Out(eight_bit_compare_21_out));
  Register #(.trigger("falling")) ACC (
    .D(multiplexer_6_out), .en(1'b1), .clk(or_10_out), .Q(ACC_q), .clr(button_2_out));
  or or_10 (or_10_out, and_9_out, eight_bit_compare_18_out, eight_bit_compare_20_out);
  D_Flip_Flop #(.trigger("falling")) Carry (.D(alu_1_co), .clk(or_11_out), .Q(Carry_q));  // open: Qn, preset, reset
  or or_11 (or_11_out, eight_bit_compare_17_out, eight_bit_compare_16_out, eight_bit_compare_21_out);

  // Notes on the sheet:
  //   11 STO A
  //   RM bit
  //   Clear
  //   13 STO B
  //   ACC
  //   LOD SP 14
  //   Program Counter
  //   MDR
  //   MOV SP, A
  //   FF HLT
  //   Only saves on next opcode
  //   34 JNC
  //   33 JNZ
  //   32 JC
  //   31 JZ
  //   30 JMP
  //   STO SP, A
  //   LOD B 12
  //   16 LOD B SP 
  //   MDR
  //   ACC
  //   41 MOV B, A
  //   8 bit code
  //   8 bit address
  //   8 bit data
  //   ADD or SUB
  //   42 MOV A, SP
  //   ADD 20, SUB 21, LOD A 10, ADC 22
  //   B
  //   40 MOV A, B
endmodule

module Eight_Bit_Counter (
  input  Set,
  input  [7:0] DI,
  input  Clear,
  input  Clock,
  output [7:0] out_5
);

  wire [7:0] alu_1_so, multiplexer_1_out;

  ALU alu_1 (.A(8'h1), .B(out_5), .Sub(1'b0), .SO(alu_1_so));  // open: CO, CI
  Multiplexer #(.width(8), .enable("false")) multiplexer_1 (
    .in0(alu_1_so), .in1(DI), .out(multiplexer_1_out), .sel(Set));
  Register register_1 (.D(multiplexer_1_out), .en(1'b1), .clk(Clock), .Q(out_5), .clr(Clear));

  // Notes on the sheet:
  //   From this point and onwards, because I've already established how 8 bit latches and RAM are built, I will be using the one in the software for convenience in debugging
endmodule

module Eight_Bit_Compare (
  input  [7:0] A,
  input  [7:0] B,
  output Out
);

  wire xnor_1_out, xnor_2_out, xnor_3_out, xnor_4_out, xnor_5_out, xnor_6_out, xnor_7_out, xnor_8_out;

  xnor xnor_1 (xnor_1_out, A[0], B[0]);
  xnor xnor_2 (xnor_2_out, A[1], B[1]);
  xnor xnor_3 (xnor_3_out, A[2], B[2]);
  xnor xnor_4 (xnor_4_out, A[3], B[3]);
  xnor xnor_5 (xnor_5_out, A[4], B[4]);
  xnor xnor_6 (xnor_6_out, A[5], B[5]);
  xnor xnor_7 (xnor_7_out, A[6], B[6]);
  xnor xnor_8 (xnor_8_out, A[7], B[7]);
  and and_1 (Out, xnor_1_out, xnor_2_out, xnor_3_out, xnor_4_out, xnor_5_out, xnor_6_out, xnor_7_out, xnor_8_out);
endmodule
